# Fritzing sketch HomeEnvironment_i2c_first_version (saved by Fritzing 0.9.3b)
stripboards: 2

parts:
  U1 = ESP8266-12e_tht [part_number=ESP8266-12E]
  TSL2561 = IC, SIP package, 5 pins [chip_label=IC]
  BMP180 = IC, SIP package, 4 pins [chip_label=IC]
  CCS811 = IC, SIP package, 8 pins [chip_label=IC]
  MAX4466 = IC, SIP package, 3 pins [chip_label=IC]
  Arduino1 = Arduino Pro Mini (3.3V)
  DHT22 = IC, SIP package, 4 pins [chip_label=IC]
  PIR = IC, SIP package, 3 pins [chip_label=IC]
  PPD42 = IC, SIP package, 5 pins [chip_label=IC]
  MH-Z19 = IC, SIP package, 9 pins [chip_label=IC]
  R1 = Resistor [tolerance=±5% resistance=10k package=THT]
  R2 = Resistor [tolerance=±5% resistance=10k package=THT]
  R3 = Resistor [tolerance=±5% resistance=10k package=THT]
  R4 = Resistor [tolerance=±5% resistance=10k package=THT]
  Program = female pin header, 3 pins [form="♀ (female)"]
  C1 = Electrolytic Capacitor [capacitance=100µF package="100 mil [THT, electrolytic]"]
  C2 = Ceramic Capacitor [capacitance=100nF package="100 mil [THT, multilayer]"]

nets:
  N1: U1.REST, R2.Pin_1
  N2: U1.CH_PD, R1.Pin_1
  N3: U1.GPIO_16, PIR.pin2
  N4: U1.GPIO_12, Arduino1.D2
  3.3V: U1.VCC, TSL2561.pin1, BMP180.pin4, CCS811.pin1, PIR.pin3, R1.Pin_0, R2.Pin_0, R3.Pin_0
  GND: U1.GND, TSL2561.pin2, BMP180.pin3, CCS811.pin2, CCS811.pin5, Arduino1.GND, PIR.pin1, MH-Z19.pin7, R4.Pin_1
  N5: U1.GPIO_15, R4.Pin_0
  N6: U1.GPIO_0, R3.Pin_1
  N7: U1.GPIO_4, TSL2561.pin4, BMP180.pin1, CCS811.pin4, Arduino1.A4
  N8: U1.GPIO_5, TSL2561.pin3, BMP180.pin2, CCS811.pin3, Arduino1.A5
  N9: U1.GPIO_3/RXD, Program.pin3
  N10: U1.GPIO_1/TXD, Program.pin2
  N11: MAX4466.pin1, Arduino1.A0
  N12: MAX4466.pin2, DHT22.pin4, PPD42.pin1, C1.-, C2.0
  N13: MAX4466.pin3, Arduino1.A1, C1.+, C2.1
  N14: Arduino1.VCC, DHT22.pin1
  N15: Arduino1.D9, MH-Z19.pin2
  N16: Arduino1.D8, MH-Z19.pin3
  N17: Arduino1.D4, DHT22.pin2
  N18: Arduino1.D3, PPD42.pin4
  5V: PPD42.pin3, MH-Z19.pin6

notes:
  I2C

custom parts:
  ESP8266-12e_tht: These are the first series of modules made with the ESP8266 by the third-party manufacturer AI-Thinker and remain the most widely available. They are collectively referred to as "ESP-xx modules" and to form a workable development system require additional components, especially a serial TTL-to-USB adapter (sometimes called a USB-to-UART bridge) and an external 3.3V power supply. The pcb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
