# Fritzing sketch HomeEnvironment_i2c_low_power_version (saved by Fritzing 0.9.3b)
stripboards: 2

parts:
  part = ESP8266-12e_tht [part_number=ESP8266-12E]
  TSL2561 = IC, SIP package, 5 pins
  BMP180 = IC, SIP package, 4 pins
  CCS811 = IC, SIP package, 8 pins
  MAX4466 = IC, SIP package, 3 pins
  Arduino1 = Arduino Pro Mini (3.3V)
  DHT22 = IC, SIP package, 4 pins
  PIR = IC, SIP package, 3 pins
  PPD42 = IC, SIP package, 5 pins
  part_2 = Resistor [tolerance=±5% resistance=10k package=THT]
  part_3 = Resistor [tolerance=±5% resistance=10k package=THT]
  part_4 = Resistor [tolerance=±5% resistance=10k package=THT]
  Program = female pin header, 3 pins [form="♀ (female)"]
  part_5 = Electrolytic Capacitor [capacitance=100µF package="100 mil [THT, electrolytic]"]
  part_6 = Ceramic Capacitor [capacitance=100nF package="100 mil [THT, multilayer]"]
  Reset = female pin header, 1 pin [form="♀ (female)"]
  part_7 = Electrolytic Capacitor [capacitance=47µF package="100 mil [THT, electrolytic]"]  # not connected
  part_8 = Resistor [tolerance=±5% resistance=10k package=THT]

nets:
  N1: part.REST, Arduino1.D8, Reset.pin1, part_8.Pin_1
  N2: part.CH_PD, part_2.Pin_1
  3.3V: part.VCC, TSL2561.pin1, BMP180.pin4, CCS811.pin1, Arduino1.VCC, DHT22.pin1, PIR.pin3, part_2.Pin_0, part_3.Pin_0, part_8.Pin_0
  GND: part.GND, TSL2561.pin2, BMP180.pin3, CCS811.pin2, CCS811.pin5, Arduino1.GND, PIR.pin1
  N3: part.GPIO_15, part_4.Pin_0
  N4: part.GPIO_0, part_3.Pin_1
  N5: part.GPIO_4, TSL2561.pin4, BMP180.pin1, CCS811.pin4, Arduino1.A4
  N6: part.GPIO_5, TSL2561.pin3, BMP180.pin2, CCS811.pin3, Arduino1.A5
  N7: part.GPIO_3/RXD, Program.pin3
  N8: part.GPIO_1/TXD, Program.pin2
  N9: MAX4466.pin1, Arduino1.A0
  N10: MAX4466.pin2, DHT22.pin4, PPD42.pin1, part_5.-, part_6.0
  N11: MAX4466.pin3, Arduino1.A1, part_5.+, part_6.1
  N12: Arduino1.D9, PIR.pin2
  N13: Arduino1.D4, DHT22.pin2
  N14: Arduino1.D3, PPD42.pin4
  5V: PPD42.pin3

notes:
  I2C
  Wakeup

custom parts:
  ESP8266-12e_tht: These are the first series of modules made with the ESP8266 by the third-party manufacturer AI-Thinker and remain the most widely available. They are collectively referred to as "ESP-xx modules" and to form a workable development system require additional components, especially a serial TTL-to-USB adapter (sometimes called a USB-to-UART bridge) and an external 3.3V power supply. The pcb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
