# Fritzing sketch HomeEnvironment_spi_version (saved by Fritzing 0.9.3b)
breadboards: 1

parts:
  TSL2561 = IC, SIP package, 5 pins
  BMP180 = IC, SIP package, 4 pins
  CCS811 = IC, SIP package, 8 pins
  MAX4466 = IC, SIP package, 3 pins
  DHT22 = IC, SIP package, 4 pins
  PIR = IC, SIP package, 3 pins
  PPD42 = IC, SIP package, 5 pins
  Arduino1 = Arduino Pro Mini (3.3V)
  U1 = ESP8266-12e_tht
  MH-Z19 = IC, SIP package, 9 pins

nets:
  3.3V: TSL2561.pin1, BMP180.pin4, CCS811.pin1, MAX4466.pin3, DHT22.pin1, PIR.pin3, Arduino1.VCC, U1.VCC
  GND: TSL2561.pin2, BMP180.pin3, CCS811.pin2, CCS811.pin5, MAX4466.pin2, DHT22.pin4, PIR.pin1, PPD42.pin1, Arduino1.GND, U1.GND, MH-Z19.pin7
  N1: TSL2561.pin3, BMP180.pin2, CCS811.pin3, U1.GPIO_5
  N2: TSL2561.pin4, BMP180.pin1, CCS811.pin4, U1.GPIO_4
  N3: MAX4466.pin1, Arduino1.A0
  N4: DHT22.pin2, Arduino1.D4
  N5: PIR.pin2, U1.GPIO_16
  5V: PPD42.pin3, MH-Z19.pin6
  N6: PPD42.pin4, Arduino1.D3
  N7: Arduino1.SCK, U1.GPIO_14
  N8: Arduino1.MISO, U1.GPIO_12
  N9: Arduino1.MOSI, U1.GPIO_13
  N10: Arduino1.D10, U1.GPIO_15
  N11: Arduino1.D7, MH-Z19.pin3
  N12: Arduino1.D6, MH-Z19.pin2

notes:
  SPI

custom parts:
  ESP8266-12e_tht: These are the first series of modules made with the ESP8266 by the third-party manufacturer AI-Thinker and remain the most widely available. They are collectively referred to as "ESP-xx modules" and to form a workable development system require additional components, especially a serial TTL-to-USB adapter (sometimes called a USB-to-UART bridge) and an external 3.3V power supply. The pcb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
